// Logisim project 2.a.circ as structural Verilog: 1 circuit, main circuit main
module main (
  input  A,
  input  B,
  input  C,
  output T
);

  wire AB_out, AC_out, BC_out;

  and AB (AB_out, A, B);
  and AC (AC_out, A, C);
  and BC (BC_out, B, C);
  or OR (T, AB_out, AC_out, BC_out);
endmodule
