// Logisim project 2.b.circ as structural Verilog: 1 circuit, main circuit main
module main (
  input  A,
  input  B,
  input  C,
  output S
);

  wire A_nB_nC_out, ABC_out, nA_B_nC_out, nA_nB_C_out;

  and nA_nB_C (nA_nB_C_out, ~A, ~B, C);  // AND_Gate
  and nA_B_nC (nA_B_nC_out, ~A, B, ~C);  // AND_Gate
  and A_nB_nC (A_nB_nC_out, A, ~B, ~C);  // AND_Gate
  and ABC (ABC_out, A, B, C);
  or OR (S, nA_nB_C_out, nA_B_nC_out, A_nB_nC_out, ABC_out);
endmodule
